// Digital circuit 8bit_cpu.dig as structural Verilog
module _8bit_cpu (
  input  clk,
  input  Reset,
  input  Enable,
  input  Read,
  input  Reset_2,
  input  Enable_2,
  input  Read_2,
  input  Enable_3,
  input  in_9,
  input  in_10,
  input  in_11,
  input  in_12,
  input  in_13,
  input  in_14,
  input  in_15,
  input  in_16,
  input  Sub
);

  wire _7486_1_pin3, _7486_1_pin6, _7486_1_pin8, _7486_1_pin11, _7486_2_pin3, _7486_2_pin6, _7486_2_pin8,
       _7486_2_pin11, _74173_1_pin3, _74173_1_pin4, _74173_1_pin5, _74173_1_pin6, _74173_2_pin3,
       _74173_2_pin4, _74173_2_pin5, _74173_2_pin6, _74245_1_pin2, _74245_1_pin3, _74245_1_pin4,
       _74245_1_pin5, _74245_1_pin6, _74245_1_pin7, _74245_1_pin8, _74245_1_pin9, _74245_2_pin6,
       _74245_2_pin7, _74245_2_pin8, _74245_2_pin9, _74245_3_pin6, _74245_3_pin7, _74245_3_pin8,
       _74245_3_pin9, _74283_1_pin7;

  // PolarityAwareLED polarityawareled_1: pin names not known; wires that end beside it: 1'b0, in_9
  // PolarityAwareLED polarityawareled_2: pin names not known; wires that end beside it: 1'b0, in_10
  // PolarityAwareLED polarityawareled_3: pin names not known; wires that end beside it: 1'b0, in_11
  // PolarityAwareLED polarityawareled_4: pin names not known; wires that end beside it: 1'b0, in_12
  // PolarityAwareLED polarityawareled_5: pin names not known; wires that end beside it: 1'b0, in_13
  // PolarityAwareLED polarityawareled_6: pin names not known; wires that end beside it: 1'b0, in_14
  // PolarityAwareLED polarityawareled_7: pin names not known; wires that end beside it: 1'b0, in_15
  // PolarityAwareLED polarityawareled_8: pin names not known; wires that end beside it: 1'b0, in_16
  _74245 _74245_1 (
    .pin1(1'b1), .pin2(_74245_1_pin2), .pin3(_74245_1_pin3), .pin4(_74245_1_pin4), .pin5(_74245_1_pin5),
    .pin6(_74245_1_pin6), .pin7(_74245_1_pin7), .pin8(_74245_1_pin8), .pin9(_74245_1_pin9), .pin10(1'b0),
    .pin11(in_16), .pin12(in_15), .pin13(in_14), .pin14(in_13), .pin15(in_12), .pin16(in_11), .pin17(in_10),
    .pin18(in_9), .pin19(Enable_3), .pin20(1'b1));
  // PolarityAwareLED polarityawareled_9: pin names not known; wires that end beside it: _74245_1_pin2, 1'b0
  // PolarityAwareLED polarityawareled_10: pin names not known; wires that end beside it: _74245_1_pin3, 1'b0
  // PolarityAwareLED polarityawareled_11: pin names not known; wires that end beside it: _74245_1_pin4, 1'b0
  _74173 _74173_1 (
    .pin1(1'b0), .pin2(1'b0), .pin3(_74173_1_pin3), .pin4(_74173_1_pin4), .pin5(_74173_1_pin5),
    .pin6(_74173_1_pin6), .pin7(clk), .pin8(1'b0), .pin9(Read_2), .pin10(Read_2), .pin11(in_12),
    .pin12(in_11), .pin13(in_10), .pin14(in_9), .pin15(Reset_2), .pin16(1'b1));
  // PolarityAwareLED polarityawareled_12: pin names not known; wires that end beside it: _74245_1_pin5, 1'b0
  // PolarityAwareLED polarityawareled_13: pin names not known; wires that end beside it: _74245_1_pin6, 1'b0
  _74173 _74173_2 (
    .pin1(1'b0), .pin2(1'b0), .pin3(_74173_2_pin3), .pin4(_74173_2_pin4), .pin5(_74173_2_pin5),
    .pin6(_74173_2_pin6), .pin7(clk), .pin8(1'b0), .pin9(Read), .pin10(Read), .pin11(in_12), .pin12(in_11),
    .pin13(in_10), .pin14(in_9), .pin15(Reset), .pin16(1'b1));
  // PolarityAwareLED polarityawareled_14: pin names not known; wires that end beside it: _74245_1_pin7, 1'b0
  // PolarityAwareLED polarityawareled_15: pin names not known; wires that end beside it: _74245_1_pin8, 1'b0
  // PolarityAwareLED polarityawareled_16: pin names not known; wires that end beside it: _74245_1_pin9, 1'b0
  _74245 _74245_2 (
    .pin1(1'b1), .pin2(_74173_1_pin3), .pin3(_74173_1_pin4), .pin4(_74173_1_pin5), .pin5(_74173_1_pin6),
    .pin6(_74245_2_pin6), .pin7(_74245_2_pin7), .pin8(_74245_2_pin8), .pin9(_74245_2_pin9), .pin10(1'b0),
    .pin11(in_16), .pin12(in_15), .pin13(in_14), .pin14(in_13), .pin15(in_12), .pin16(in_11), .pin17(in_10),
    .pin18(in_9), .pin19(Enable_2), .pin20(1'b1));
  // PolarityAwareLED polarityawareled_17: pin names not known; wires that end beside it: _74173_1_pin3, 1'b0
  _7486 _7486_1 (
    .pin1(_74173_2_pin3), .pin2(Sub), .pin3(_7486_1_pin3), .pin4(_74173_2_pin4), .pin5(Sub),
    .pin6(_7486_1_pin6), .pin7(1'b0), .pin8(_7486_1_pin8), .pin9(_74173_2_pin5), .pin10(Sub),
    .pin11(_7486_1_pin11), .pin12(_74173_2_pin6), .pin13(Sub), .pin14(1'b1));
  _74245 _74245_3 (
    .pin1(1'b1), .pin2(_74173_2_pin3), .pin3(_74173_2_pin4), .pin4(_74173_2_pin5), .pin5(_74173_2_pin6),
    .pin6(_74245_3_pin6), .pin7(_74245_3_pin7), .pin8(_74245_3_pin8), .pin9(_74245_3_pin9), .pin10(1'b0),
    .pin11(in_16), .pin12(in_15), .pin13(in_14), .pin14(in_13), .pin15(in_12), .pin16(in_11), .pin17(in_10),
    .pin18(in_9), .pin19(Enable), .pin20(1'b1));
  // PolarityAwareLED polarityawareled_18: pin names not known; wires that end beside it: _74173_2_pin3, 1'b0
  // PolarityAwareLED polarityawareled_19: pin names not known; wires that end beside it: _74173_1_pin4, 1'b0
  // PolarityAwareLED polarityawareled_20: pin names not known; wires that end beside it: _74173_1_pin5, 1'b0
  // PolarityAwareLED polarityawareled_21: pin names not known; wires that end beside it: _74173_2_pin4, 1'b0
  // PolarityAwareLED polarityawareled_22: pin names not known; wires that end beside it: _74173_2_pin5, 1'b0
  // PolarityAwareLED polarityawareled_23: pin names not known; wires that end beside it: _74173_1_pin6, 1'b0
  // PolarityAwareLED polarityawareled_24: pin names not known; wires that end beside it: _74245_2_pin6, 1'b0
  _74283 _74283_1 (
    .pin1(_74245_1_pin4), .pin2(_7486_1_pin8), .pin3(_74173_1_pin5), .pin4(_74245_1_pin5),
    .pin5(_74173_1_pin6), .pin6(_7486_1_pin11), .pin7(_74283_1_pin7), .pin8(1'b0), .pin10(_74245_1_pin2),
    .pin11(_7486_1_pin3), .pin12(_74173_1_pin3), .pin13(_74245_1_pin3), .pin14(_74173_1_pin4),
    .pin15(_7486_1_pin6), .pin16(1'b1));  // open: pin9
  // PolarityAwareLED polarityawareled_25: pin names not known; wires that end beside it: _74173_2_pin6, 1'b0
  // PolarityAwareLED polarityawareled_26: pin names not known; wires that end beside it: _74245_3_pin6, 1'b0
  // PolarityAwareLED polarityawareled_27: pin names not known; wires that end beside it: _74245_2_pin7, 1'b0
  // PolarityAwareLED polarityawareled_28: pin names not known; wires that end beside it: _74245_2_pin8, 1'b0
  // PolarityAwareLED polarityawareled_29: pin names not known; wires that end beside it: _74245_3_pin7, 1'b0
  // PolarityAwareLED polarityawareled_30: pin names not known; wires that end beside it: _74245_3_pin8, 1'b0
  // PolarityAwareLED polarityawareled_31: pin names not known; wires that end beside it: _74245_2_pin9, 1'b0
  // PolarityAwareLED polarityawareled_32: pin names not known; wires that end beside it: _74245_3_pin9, 1'b0
  _74173 _74173_3 (
    .pin1(1'b0), .pin2(1'b0), .pin3(_74245_2_pin6), .pin4(_74245_2_pin7), .pin5(_74245_2_pin8),
    .pin6(_74245_2_pin9), .pin7(clk), .pin8(1'b0), .pin9(Read_2), .pin10(Read_2), .pin11(in_16),
    .pin12(in_15), .pin13(in_14), .pin14(in_13), .pin15(Reset_2), .pin16(1'b1));
  _74173 _74173_4 (
    .pin1(1'b0), .pin2(1'b0), .pin3(_74245_3_pin6), .pin4(_74245_3_pin7), .pin5(_74245_3_pin8),
    .pin6(_74245_3_pin9), .pin7(clk), .pin8(1'b0), .pin9(Read), .pin10(Read), .pin11(in_16), .pin12(in_15),
    .pin13(in_14), .pin14(in_13), .pin15(Reset), .pin16(1'b1));
  _7486 _7486_2 (
    .pin1(_74245_3_pin6), .pin2(Sub), .pin3(_7486_2_pin3), .pin4(_74245_3_pin7), .pin5(Sub),
    .pin6(_7486_2_pin6), .pin7(1'b0), .pin8(_7486_2_pin8), .pin9(_74245_3_pin8), .pin10(Sub),
    .pin11(_7486_2_pin11), .pin12(_74245_3_pin9), .pin13(Sub), .pin14(1'b1));
  _74283 _74283_2 (
    .pin1(_74245_1_pin8), .pin2(_7486_2_pin8), .pin3(_74245_2_pin8), .pin4(_74245_1_pin9),
    .pin5(_74245_2_pin9), .pin6(_7486_2_pin11), .pin7(Sub), .pin8(1'b0), .pin9(_74283_1_pin7),
    .pin10(_74245_1_pin6), .pin11(_7486_2_pin3), .pin12(_74245_2_pin6), .pin13(_74245_1_pin7),
    .pin14(_74245_2_pin7), .pin15(_7486_2_pin6), .pin16(1'b1));

  // Notes on the sheet:
  //   clk: Hz: 100
  //   Enable: default 1
  //   Read: default 1
  //   Enable_2: default 1
  //   Read_2: default 1
  //   Enable_3: default 1
endmodule
