// Digital circuit 8bit_alu.dig as structural Verilog
module _8bit_alu (
  input  SO,
  input  SUB,
  output B0,
  output B1,
  output B2,
  output B3,
  output B4,
  output B5,
  output B6,
  output B7,
  output A0,
  output A1,
  output A2,
  output A3,
  output A4,
  output A5,
  output A6,
  output A7,
  output Val0,
  output Val1,
  output Val2,
  output Val3,
  output Val4,
  output Val5,
  output Val6,
  output Val7,
  output O0,
  output O1,
  output O2,
  output O3,
  output O4,
  output O5,
  output O6,
  output O7
);

  wire _7486_1_pin3, _7486_1_pin6, _7486_1_pin8, _7486_1_pin11, _7486_2_pin3, _7486_2_pin6, _7486_2_pin8,
       _7486_2_pin11, _74283_1_pin7;

  _74245 _74245_1 (
    .pin1(1'b1), .pin2(Val7), .pin3(Val6), .pin4(Val5), .pin5(Val4), .pin6(Val3), .pin7(Val2), .pin8(Val1),
    .pin9(Val0), .pin10(1'b0), .pin11(O0), .pin12(O1), .pin13(O2), .pin14(O3), .pin15(O4), .pin16(O5),
    .pin17(O6), .pin18(O7), .pin19(SO), .pin20(1'b1));
  _7486 _7486_1 (
    .pin1(B7), .pin2(SUB), .pin3(_7486_1_pin3), .pin4(B6), .pin5(SUB), .pin6(_7486_1_pin6), .pin7(1'b0),
    .pin8(_7486_1_pin8), .pin9(B5), .pin10(SUB), .pin11(_7486_1_pin11), .pin12(B4), .pin13(SUB), .pin14(1'b1));
  _74283 _74283_1 (
    .pin1(Val5), .pin2(_7486_1_pin8), .pin3(A5), .pin4(Val4), .pin5(A4), .pin6(_7486_1_pin11),
    .pin7(_74283_1_pin7), .pin8(1'b0), .pin10(Val7), .pin11(_7486_1_pin3), .pin12(A7), .pin13(Val6),
    .pin14(A6), .pin15(_7486_1_pin6), .pin16(1'b1));  // open: pin9
  _7486 _7486_2 (
    .pin1(B3), .pin2(SUB), .pin3(_7486_2_pin3), .pin4(B2), .pin5(SUB), .pin6(_7486_2_pin6), .pin7(1'b0),
    .pin8(_7486_2_pin8), .pin9(B1), .pin10(SUB), .pin11(_7486_2_pin11), .pin12(B0), .pin13(SUB), .pin14(1'b1));
  _74283 _74283_2 (
    .pin1(Val1), .pin2(_7486_2_pin8), .pin3(A1), .pin4(Val0), .pin5(A0), .pin6(_7486_2_pin11), .pin7(SUB),
    .pin8(1'b0), .pin9(_74283_1_pin7), .pin10(Val3), .pin11(_7486_2_pin3), .pin12(A3), .pin13(Val2),
    .pin14(A2), .pin15(_7486_2_pin6), .pin16(1'b1));
endmodule
