// Digital circuit 8bit_cpu.dig as structural Verilog
module _8bit_cpu (
  input  BC,
  input  BO,
  input  BI,
  input  AC,
  input  AO,
  input  AI,
  input  SO,
  input  in_8,
  input  in_9,
  input  in_10,
  input  in_11,
  input  in_12,
  input  in_13,
  input  in_14,
  input  in_15,
  input  SUB,
  input  CLOCK
);

  wire _8bit_alu_1_a0, _8bit_alu_1_a1, _8bit_alu_1_a2, _8bit_alu_1_val0, _8bit_alu_1_val1, _8bit_alu_1_val2,
       _8bit_alu_1_val3, _8bit_alu_1_val4, not_1_out, not_2_out, not_3_out, not_4_out, not_5_out,
       polarityawareled_9_p1, polarityawareled_10_p1, polarityawareled_11_p1, polarityawareled_12_p1,
       polarityawareled_13_p1, polarityawareled_14_p1, polarityawareled_15_p1, polarityawareled_16_p1,
       polarityawareled_19_p1, polarityawareled_20_p1, RegB_o0, RegB_o1, RegB_o2, RegB_o3, RegB_o4, RegB_o5;

  // PolarityAwareLED polarityawareled_1: pin names not known; wires that end beside it: 1'b0, in_8
  PullDown pulldown_1 (.out(in_8));
  // PolarityAwareLED polarityawareled_2: pin names not known; wires that end beside it: 1'b0, in_9
  // PolarityAwareLED polarityawareled_3: pin names not known; wires that end beside it: 1'b0, in_10
  PullDown pulldown_2 (.out(in_9));
  PullDown pulldown_3 (.out(in_10));
  // PolarityAwareLED polarityawareled_4: pin names not known; wires that end beside it: 1'b0, in_11
  // PolarityAwareLED polarityawareled_5: pin names not known; wires that end beside it: 1'b0, in_12
  PullDown pulldown_4 (.out(in_11));
  PullDown pulldown_5 (.out(in_12));
  // PolarityAwareLED polarityawareled_6: pin names not known; wires that end beside it: 1'b0, in_13
  // PolarityAwareLED polarityawareled_7: pin names not known; wires that end beside it: 1'b0, in_14
  PullDown pulldown_6 (.out(in_13));
  PullDown pulldown_7 (.out(in_14));
  // PolarityAwareLED polarityawareled_8: pin names not known; wires that end beside it: 1'b0, in_15
  PullDown pulldown_8 (.out(in_15));
  // PolarityAwareLED polarityawareled_9: pin names not known; wires that end beside it: polarityawareled_9_p1, 1'b0
  // PolarityAwareLED polarityawareled_10: pin names not known; wires that end beside it: polarityawareled_10_p1, 1'b0
  // PolarityAwareLED polarityawareled_11: pin names not known; wires that end beside it: polarityawareled_11_p1, 1'b0
  // PolarityAwareLED polarityawareled_12: pin names not known; wires that end beside it: polarityawareled_12_p1, 1'b0
  // PolarityAwareLED polarityawareled_13: pin names not known; wires that end beside it: polarityawareled_13_p1, 1'b0
  // PolarityAwareLED polarityawareled_14: pin names not known; wires that end beside it: polarityawareled_14_p1, 1'b0
  // PolarityAwareLED polarityawareled_15: pin names not known; wires that end beside it: polarityawareled_15_p1, 1'b0
  // PolarityAwareLED polarityawareled_16: pin names not known; wires that end beside it: polarityawareled_16_p1, 1'b0
  _8bit_register RegB (
    .O(not_4_out), .R(not_5_out), .CLR(BC), .CLK(CLOCK), .O7(polarityawareled_12_p1),
    .O6(polarityawareled_11_p1), .O5(RegB_o5), .O4(RegB_o4), .O3(RegB_o3), .O2(RegB_o2), .O1(RegB_o1),
    .O0(RegB_o0), .I7(in_8), .I6(in_9), .I5(in_10), .I4(in_11), .I3(in_12), .I2(in_13), .I1(in_14), .I0(in_15));
  // PolarityAwareLED polarityawareled_17: pin names not known; wires that end beside it: RegB_o4, 1'b0
  // PolarityAwareLED polarityawareled_18: pin names not known; wires that end beside it: RegB_o5, 1'b0
  // PolarityAwareLED polarityawareled_19: pin names not known; wires that end beside it: polarityawareled_19_p1, 1'b0
  // PolarityAwareLED polarityawareled_20: pin names not known; wires that end beside it: polarityawareled_20_p1, 1'b0
  _8bit_ALU _8bit_alu_1 (
    .Val7(polarityawareled_10_p1), .Val6(polarityawareled_15_p1), .Val5(polarityawareled_16_p1),
    .Val4(_8bit_alu_1_val4), .Val3(_8bit_alu_1_val3), .Val2(_8bit_alu_1_val2), .Val1(_8bit_alu_1_val1),
    .Val0(_8bit_alu_1_val0), .B7(polarityawareled_12_p1), .B6(polarityawareled_11_p1), .B5(RegB_o5),
    .B4(RegB_o4), .B3(RegB_o3), .B2(RegB_o2), .B1(RegB_o1), .B0(RegB_o0), .O7(in_8), .O6(in_9), .O5(in_10),
    .O4(in_11), .O3(in_12), .O2(in_13), .O1(in_14), .O0(in_15), .A7(polarityawareled_9_p1),
    .A6(polarityawareled_14_p1), .A5(polarityawareled_13_p1), .A4(polarityawareled_20_p1),
    .A3(polarityawareled_19_p1), .A2(_8bit_alu_1_a2), .A1(_8bit_alu_1_a1), .A0(_8bit_alu_1_a0),
    .SO(not_3_out), .SUB(SUB));
  // PolarityAwareLED polarityawareled_21: pin names not known; wires that end beside it: _8bit_alu_1_val3, 1'b0
  // PolarityAwareLED polarityawareled_22: pin names not known; wires that end beside it: _8bit_alu_1_val4, 1'b0
  // PolarityAwareLED polarityawareled_23: pin names not known; wires that end beside it: RegB_o2, 1'b0
  // PolarityAwareLED polarityawareled_24: pin names not known; wires that end beside it: RegB_o3, 1'b0
  // PolarityAwareLED polarityawareled_25: pin names not known; wires that end beside it: _8bit_alu_1_a1, 1'b0
  // PolarityAwareLED polarityawareled_26: pin names not known; wires that end beside it: _8bit_alu_1_a2, 1'b0
  // PolarityAwareLED polarityawareled_27: pin names not known; wires that end beside it: _8bit_alu_1_val1, 1'b0
  // PolarityAwareLED polarityawareled_28: pin names not known; wires that end beside it: _8bit_alu_1_val2, 1'b0
  // PolarityAwareLED polarityawareled_29: pin names not known; wires that end beside it: RegB_o0, 1'b0
  // PolarityAwareLED polarityawareled_30: pin names not known; wires that end beside it: RegB_o1, 1'b0
  _8bit_register RegA (
    .O(not_1_out), .R(not_2_out), .CLR(AC), .CLK(CLOCK), .O7(polarityawareled_9_p1),
    .O6(polarityawareled_14_p1), .O5(polarityawareled_13_p1), .O4(polarityawareled_20_p1),
    .O3(polarityawareled_19_p1), .O2(_8bit_alu_1_a2), .O1(_8bit_alu_1_a1), .O0(_8bit_alu_1_a0), .I7(in_8),
    .I6(in_9), .I5(in_10), .I4(in_11), .I3(in_12), .I2(in_13), .I1(in_14), .I0(in_15));
  // PolarityAwareLED polarityawareled_31: pin names not known; wires that end beside it: _8bit_alu_1_a0, 1'b0
  // PolarityAwareLED polarityawareled_32: pin names not known; wires that end beside it: _8bit_alu_1_val0, 1'b0
  not not_1 (not_1_out, AO);
  not not_2 (not_2_out, AI);
  not not_3 (not_3_out, SO);
  not not_4 (not_4_out, BO);
  not not_5 (not_5_out, BI);
  // PolarityAwareLED polarityawareled_33: pin names not known; wires that end beside it: 1'b0, AO
  // PolarityAwareLED polarityawareled_34: pin names not known; wires that end beside it: 1'b0, AI
  // PolarityAwareLED polarityawareled_35: pin names not known; wires that end beside it: 1'b0, AC
  // PolarityAwareLED polarityawareled_36: pin names not known; wires that end beside it: 1'b0, SO
  // PolarityAwareLED polarityawareled_37: pin names not known; wires that end beside it: 1'b0, SUB
  // PolarityAwareLED polarityawareled_38: pin names not known; wires that end beside it: 1'b0, BO
  // PolarityAwareLED polarityawareled_39: pin names not known; wires that end beside it: 1'b0, BI
  // PolarityAwareLED polarityawareled_40: pin names not known; wires that end beside it: 1'b0, BC

  // Notes on the sheet:
  //   CLOCK: Hz: 5
endmodule
