// Digital circuit 8bit_register.dig as structural Verilog
module _8bit_register (
  input  R,
  input  O,
  input  CLR,
  input  CLK,
  output O7,
  output O6,
  output O5,
  output O4,
  output O3,
  output O2,
  output O1,
  output O0,
  output I0,
  output I1,
  output I2,
  output I3,
  output I4,
  output I5,
  output I6,
  output I7
);

  _74173 _74173_1 (
    .pin1(1'b0), .pin2(1'b0), .pin3(O7), .pin4(O6), .pin5(O5), .pin6(O4), .pin7(CLK), .pin8(1'b0), .pin9(R),
    .pin10(R), .pin11(I4), .pin12(I5), .pin13(I6), .pin14(I7), .pin15(CLR), .pin16(1'b1));
  _74245 _74245_1 (
    .pin1(1'b1), .pin2(O7), .pin3(O6), .pin4(O5), .pin5(O4), .pin6(O3), .pin7(O2), .pin8(O1), .pin9(O0),
    .pin10(1'b0), .pin11(I0), .pin12(I1), .pin13(I2), .pin14(I3), .pin15(I4), .pin16(I5), .pin17(I6),
    .pin18(I7), .pin19(O), .pin20(1'b1));
  _74173 _74173_2 (
    .pin1(1'b0), .pin2(1'b0), .pin3(O3), .pin4(O2), .pin5(O1), .pin6(O0), .pin7(CLK), .pin8(1'b0), .pin9(R),
    .pin10(R), .pin11(I0), .pin12(I1), .pin13(I2), .pin14(I3), .pin15(CLR), .pin16(1'b1));
endmodule
